# Fritzing sketch primograph_schematic (saved by Fritzing 0.9.2b)

parts:
  Raspberry_Pi1 = Raspberry Pi 2  # not connected
  U1 = Explorer HAT Pro [part_number="Explorer HAT Pro" package=THT]
  S1 = Square Pushbutton
  LED1 = LEDs [package=led10mm]
  M1 = DC Motor
  M2 = DC Motor

nets:
  N1: U1.J10, U1.Ground, S1.leg1
  N2: U1.MOSI, LED1.C
  N3: U1.Motor_1-, M1.pin_1
  N4: U1.Motor_1+, M1.pin_2
  N5: U1.Motor_2-, M2.pin_1
  N6: U1.Motor_2+, M2.pin_2

custom parts:
  Explorer HAT Pro: Explorer HAT Pro with 4 Output and 4 Input connections, 4 Analog Inputs and 2 bi-directional motor channels, plus power and ground.
